# Fritzing sketch COMUNICACIÓN I2C ENTRE RASPBERRY PI Y ARDUINO (3) (saved by Fritzing 0.9.1b)
breadboards: 2

parts:
  Part1 = Arduino Uno (Rev3)
  Part2 = Arduino Mega 2560 (Rev3)
  Raspberry_Pi1 = Raspberry Pi B+
  S1 = Pushbutton [package="[THT]"]
  S2 = Pushbutton [package="[THT]"]
  T1 = LM35 Temperature Sensor [package="TO92 [THT]"]
  R1 = Photocell (LDR) [package=THT]
  R2 = Resistor [tolerance=±1% resistance=220 package=THT]
  R3 = Resistor [tolerance=±1% resistance=220 package=THT]
  R4 = Resistor [tolerance=±1% resistance=1k package=THT]

nets:
  N1: Part1.A0, R1.pin_1, R4.Pin_0
  3V3: Part1.A4/SDA, Part2.D20/SDA, Raspberry_Pi1.3v3, Raspberry_Pi1.GPIO2, Raspberry_Pi1.3V3
  N2: Part1.A5/SCL, Part2.D21/SCL, Raspberry_Pi1.GPIO3
  N3: Part1.D7, S2.Pin_1, S2.Pin_2, R3.Pin_0
  GND: Part1.GND, Part2.GND, Raspberry_Pi1.GND, T1.GND, R1.pin_0, R2.Pin_1, R3.Pin_1
  N4: Part2.A0, T1.Vout
  N5: Part2.5V, S1.Pin_3, S1.Pin_4, S2.Pin_3, S2.Pin_4, T1.+Vs, R4.Pin_1
  N6: Part2.D7_PWM, S1.Pin_1, S1.Pin_2, R2.Pin_0
